// Logisim project intro_prefabs.circ as structural Verilog: 1 circuit, main circuit main
module main (
  input  in_1,
  input  in_2,
  input  in_3,
  input  in_4
);

  wire [7:0] rom_1_data;

  // Probe on {4'b0000, in_4, in_3, in_2, in_1}
  ROM rom_1 (.addr({4'b0000, in_4, in_3, in_2, in_1}), .data(rom_1_data));
  Hex_Digit_Display hex_digit_display_1 (.value(rom_1_data[7:4]));  // open: dp
  Hex_Digit_Display hex_digit_display_2 (.value(rom_1_data[3:0]));  // open: dp
  // Probe on rom_1_data

  // Notes on the sheet:
  //   contents of rom_1 (hex, n*v repeats v):
  //   9 4f 4e 8 1e 89 1f 89 4d 57 4a 56 7f 4f 52 4e 9 e2 fa 55 1f 89 4d 8 e0 f9
endmodule
